// Logisim project module_fabio.circ as structural Verilog: 2 circuits, main circuit mul_by_2
module mul_by_2 (
  input  [3:0] in_1,
  output [3:0] out_2,
  output out_3
);


  assign out_2 = {in_1[2:0], 1'b0};
  assign out_3 = in_1[3];
endmodule

module mul_by_5 (
  input  [3:0] in_1,
  output [3:0] out_2,
  output out_3
);

  Add add_1 (.in_1({in_1[1:0], 2'b00}), .in_2(in_1), .out_3(out_2));  // open: C
  or or_1 (out_3, in_1[2], in_1[3]);
endmodule
