// Logisim project module_simon.circ as structural Verilog: 2 circuits, main circuit or
module \or  (
  input  [3:0] A,
  input  [3:0] B,
  output [3:0] R,
  output O
);

  assign R = A | B;  // OR_Gate or_1, 4 bits wide

  assign O = 1'b0;
endmodule

module \and  (
  input  [3:0] A,
  input  [3:0] B,
  output [3:0] R,
  output O
);

  assign R = A & B;  // AND_Gate and_1, 4 bits wide

  assign O = 1'b0;
endmodule
