// Logisim project module_tom.circ as structural Verilog
module plus (
  input  A1,
  input  B1,
  input  cin,
  output S4,
  output Overflow_Flag
);

  wire and_1_out, and_2_out, xor_1_out;

  and and_1 (and_1_out, B1, A1);
  xor xor_1 (xor_1_out, A1, B1);
  and and_2 (and_2_out, xor_1_out, cin);
  xor xor_2 (Overflow_Flag, xor_1_out, cin);
  or or_1 (S4, and_1_out, and_2_out);
endmodule

module minus (
  input  A1,
  input  B1,
  input  cin,
  output S5,
  output Overflow_Flag
);

  wire and_1_out, not_1_out, not_2_out, xor_1_out, xor_2_out;

  not not_1 (not_1_out, B1);
  xor xor_1 (xor_1_out, B1, A1);
  and and_1 (and_1_out, A1, not_1_out);
  xor xor_2 (xor_2_out, and_1_out, cin);
  not not_2 (not_2_out, and_1_out);
  and and_2 (Overflow_Flag, not_2_out, cin);
  or or_1 (S5, xor_1_out, xor_2_out);
endmodule

module Add (
  input  [3:0] in_1,
  input  [3:0] in_2,
  output [3:0] out_3,
  output C
);

  wire halb_1_c, voll_1_c_2, voll_2_c_2;

  halb halb_1 (.A(in_1[0]), .B(in_2[0]), .S(out_3[0]), .C(halb_1_c));
  voll voll_1 (.C(halb_1_c), .A(in_1[1]), .B(in_2[1]), .S(out_3[1]), .C_2(voll_1_c_2));
  voll voll_2 (.C(voll_1_c_2), .A(in_1[2]), .B(in_2[2]), .S(out_3[2]), .C_2(voll_2_c_2));
  voll voll_3 (.C(voll_2_c_2), .A(in_1[3]), .B(in_2[3]), .S(out_3[3]), .C_2(C));
endmodule

module Sub (
  input  [3:0] in_1,
  input  [3:0] in_2,
  output [3:0] out_3,
  output O
);

  wire not_1_out, not_2_out, not_3_out, not_4_out, not_5_out, voll_1_c_2, voll_2_c_2, voll_3_c_2, voll_4_c_2;

  not not_1 (not_1_out, 1'b0);
  not not_2 (not_2_out, in_2[0]);
  not not_3 (not_3_out, in_2[1]);
  not not_4 (not_4_out, in_2[2]);
  not not_5 (not_5_out, in_2[3]);
  voll voll_1 (.C(not_1_out), .A(in_1[0]), .B(not_2_out), .S(out_3[0]), .C_2(voll_1_c_2));
  voll voll_2 (.C(voll_1_c_2), .A(in_1[1]), .B(not_3_out), .S(out_3[1]), .C_2(voll_2_c_2));
  voll voll_3 (.C(voll_2_c_2), .A(in_1[2]), .B(not_4_out), .S(out_3[2]), .C_2(voll_3_c_2));
  voll voll_4 (.C(voll_3_c_2), .A(in_1[3]), .B(not_5_out), .S(out_3[3]), .C_2(voll_4_c_2));
  not not_6 (O, voll_4_c_2);
endmodule

module halb (
  input  A,
  input  B,
  output S,
  output C
);

  xor xor_1 (S, A, B);
  and and_1 (C, A, B);
endmodule

module voll (
  input  C,
  input  A,
  input  B,
  output S,
  output C_2
);

  wire halb_1_c, halb_1_s, halb_2_c;

  halb halb_1 (.A(A), .B(B), .S(halb_1_s), .C(halb_1_c));
  halb halb_2 (.A(C), .B(halb_1_s), .S(S), .C(halb_2_c));
  or or_1 (C_2, halb_2_c, halb_1_c);
endmodule
