// Logisim project module_yanick.circ as structural Verilog: 2 circuits, main circuit nota
module nota (
  input  [3:0] in_1,
  input  [3:0] in_2,
  output [3:0] out_3,
  output _0F
);

  not not_1 (out_3[0], in_1[0]);
  not not_2 (out_3[1], in_1[1]);
  not not_3 (out_3[2], in_1[2]);
  not not_4 (out_3[3], in_1[3]);

  assign _0F = 1'b0;
endmodule

module notb (
  input  [3:0] in_1,
  input  [3:0] in_2,
  output [3:0] out_3,
  output _0F
);

  not not_1 (out_3[0], in_2[0]);
  not not_2 (out_3[1], in_2[1]);
  not not_3 (out_3[2], in_2[2]);
  not not_4 (out_3[3], in_2[3]);

  assign _0F = 1'b0;
endmodule
