// Logisim project sadpluto_4BitALU.circ as structural Verilog: 2 circuits, main circuit 4-Bit ALU
module _4_Bit_ALU (
  input  A3,
  input  A2,
  input  A1,
  input  A0,
  input  B3,
  input  B2,
  input  B1,
  input  B0,
  input  S2,
  input  S1,
  input  S0,
  output OF,
  output R3,
  output R2,
  output R1,
  output R0
);

  wire [3:0] interface_1_segment_a, interface_1_segment_b, interface_1_segment_r;

  Hex_Digit_Display hex_digit_display_1 (.value(interface_1_segment_a), .dp(1'b0));
  Hex_Digit_Display hex_digit_display_2 (.value(interface_1_segment_b), .dp(1'b0));
  Interface interface_1 (
    .A3(A3), .R3(R3), .A2(A2), .R2(R2), .A1(A1), .R1(R1), .A0(A0), .R0(R0), .B3(B3), .B2(B2), .B1(B1),
    .B0(B0), .S2(S2), .S1(S1), .Segment_R(interface_1_segment_r), .OF(OF), .S0(S0),
    .Segment_A(interface_1_segment_a), .Segment_B(interface_1_segment_b));
  Hex_Digit_Display hex_digit_display_3 (.value(interface_1_segment_r), .dp(1'b0));

  // Notes on the sheet:
  //   Kleinprojekt Arithmetic and Logic Unit
  //   Teamname:
  //   ausgeführt von
  //   simon.waechter@students.fhnw.ch
  //   yanik.schraner@students.fhnw.ch
  //   tom.ohme@students.fhnw.ch
  //   fabio.strappazzon@students.fhnw.ch
  //   Sad Pluto
endmodule

module Interface (
  input  A3,
  input  A2,
  input  A1,
  input  A0,
  input  B3,
  input  B2,
  input  B1,
  input  B0,
  input  S2,
  input  S1,
  input  S0,
  output [3:0] Segment_A,
  output [3:0] Segment_B,
  output OF,
  output R3,
  output R2,
  output R1,
  output R0,
  output [3:0] Segment_R
);

  wire [3:0] add_1_out_3, and_1_r, mul_by_2_1_out_2, mul_by_5_1_out_2, nota_1_out_3, notb_1_out_3, or_1_r,
       sub_1_out_3;
  wire [7:4] add_1_c, and_1_o, mul_by_2_1_out_3, mul_by_5_1_out_3, nota_1__0f, notb_1__0f, or_1_o, sub_1_o;
  wire [7:5] multiplexer_1_out;

  \or  or_1 (.A({A3, A2, A1, A0}), .B({B3, B2, B1, B0}), .R(or_1_r), .O(or_1_o[4]));
  \and  and_1 (.A({A3, A2, A1, A0}), .B({B3, B2, B1, B0}), .R(and_1_r), .O(and_1_o[4]));
  nota nota_1 (.in_1({A3, A2, A1, A0}), .in_2({B3, B2, B1, B0}), .out_3(nota_1_out_3), ._0F(nota_1__0f[4]));
  notb notb_1 (.in_1({A3, A2, A1, A0}), .in_2({B3, B2, B1, B0}), .out_3(notb_1_out_3), ._0F(notb_1__0f[4]));
  Add add_1 (.in_1({A3, A2, A1, A0}), .in_2({B3, B2, B1, B0}), .out_3(add_1_out_3), .C(add_1_c[4]));
  Sub sub_1 (.out_3(sub_1_out_3), .O(sub_1_o[4]), .in_1({A3, A2, A1, A0}), .in_2({B3, B2, B1, B0}));
  mul_by_2 mul_by_2_1 (.in_1({A3, A2, A1, A0}), .out_2(mul_by_2_1_out_2), .out_3(mul_by_2_1_out_3[4]));
  mul_by_5 mul_by_5_1 (.in_1({A3, A2, A1, A0}), .out_2(mul_by_5_1_out_2), .out_3(mul_by_5_1_out_3[4]));
  Multiplexer #(.select(3), .width(8), .enable("false")) multiplexer_1 (
    .in0({or_1_o, or_1_r}), .in1({and_1_o, and_1_r}), .in2({nota_1__0f, nota_1_out_3}),
    .in3({notb_1__0f, notb_1_out_3}), .in4({add_1_c, add_1_out_3}), .in5({sub_1_o, sub_1_out_3}),
    .in6({mul_by_2_1_out_3, mul_by_2_1_out_2}), .in7({mul_by_5_1_out_3, mul_by_5_1_out_2}),
    .out({multiplexer_1_out, OF, R3, R2, R1, R0}), .sel({S2, S1, S0}));

  assign Segment_A = {A3, A2, A1, A0};
  assign Segment_B = {B3, B2, B1, B0};
  assign Segment_R = {R3, R2, R1, R0};
endmodule
