// Logisim project sadpluto_testbench_4BitALU.circ as structural Verilog
module testbench__main (
  output [2:0] S,
  output [3:0] A,
  output [3:0] B,
  output OF_Master,
  output [3:0] R_Master,
  output OF_Team,
  output [3:0] R_Team,
  output halt
);

  wire and_1_out, and_3_out, and_4_out, clock_1_out, comparator_1_eq, counter_1_carry, decoder_1_out0,
       decoder_1_out1, decoder_1_out2, decoder_1_out3, decoder_1_out4, decoder_1_out5, decoder_1_out6,
       decoder_1_out7, not_1_out;
  wire [4:0] register_1_q, register_2_q;

  Counter #(.width(11), .max('h7ff), .ongoal("continue")) counter_1 (
    .Q({S, A, B}), .carry(counter_1_carry), .clk(and_1_out));  // open: load, D, count, clr
  and and_1 (and_1_out, clock_1_out, ~halt);  // AND_Gate
  Clock clock_1 (.out(clock_1_out));
  Corner corner_1 ();
  Corner corner_2 ();
  // _4_Bit_ALU 4_bit_alu_1: pin names not known; wires that end beside it: A[3], A[2], A[1], A[0], B[3], B[2], B[1], B[0], S[2], S[1], S[0], OF_Master, R_Master[3], R_Master[2], R_Master[1], R_Master[0]
  Corner corner_3 ();
  Interface interface_1 (
    .A3(A[3]), .R3(R_Team[3]), .A2(A[2]), .R2(R_Team[2]), .A1(A[1]), .R1(R_Team[1]), .A0(A[0]),
    .R0(R_Team[0]), .B3(B[3]), .B2(B[2]), .B1(B[1]), .B0(B[0]), .S2(S[2]), .S1(S[1]), .OF(OF_Team), .S0(S[0]));  // open: Segment_R, Segment_A, Segment_B
  Corner corner_4 ();
  Register #(.width(5), .trigger("falling")) register_1 (
    .D({OF_Master, R_Master}), .Q(register_1_q), .clk(clock_1_out));  // open: en, clr
  Register #(.width(5), .trigger("falling")) register_2 (
    .D({OF_Team, R_Team}), .Q(register_2_q), .clk(clock_1_out));  // open: en, clr
  Comparator #(.width(5)) comparator_1 (.a(register_1_q), .b(register_2_q), .eq(comparator_1_eq));  // open: gt, lt
  Decoder #(.select(3), .enable("false")) decoder_1 (
    .out0(decoder_1_out0), .out1(decoder_1_out1), .out2(decoder_1_out2), .out3(decoder_1_out3),
    .out4(decoder_1_out4), .out5(decoder_1_out5), .out6(decoder_1_out6), .out7(decoder_1_out7), .sel(S));
  not not_1 (not_1_out, comparator_1_eq);
  LED Or (.in(decoder_1_out0));
  LED And_2 (.in(decoder_1_out1));
  LED nA (.in(decoder_1_out2));
  LED nB (.in(decoder_1_out3));
  LED Add (.in(decoder_1_out4));
  LED Sub (.in(decoder_1_out5));
  LED _2_A (.in(decoder_1_out6));
  LED _5_A (.in(decoder_1_out7));
  or or_2 (halt, not_1_out, counter_1_carry);
  LED TestPassed (.in(and_3_out));
  and and_3 (and_3_out, counter_1_carry, comparator_1_eq);
  LED TestFailed (.in(and_4_out));
  and and_4 (and_4_out, ~counter_1_carry, halt);  // AND_Gate

  // Notes on the sheet:
  //   Test Configuration
  //   Testing by comparison:
  //   Insert your circuit via Logisim Library within red corners.
  //   Ctrl-R to reset everything.
  //   TestPassed shows green: Circuit OK, TestFailed shows red: not OK.
  //   Test output into file via cmd-tool:
  //   java -jar "logisim-generic-2.7.1.jar" testbench4BitALU.circ -tty table > testbench4BitALUResults.log
  //   Then Ctrl-K to start counter.
  //   Selected
endmodule
